# Fritzing sketch fan_manager_basic_circuit (saved by Fritzing 0.9.3b)
breadboards: 1

parts:
  Raspberry_Pi1 = Raspberry Pi B+
  R1 = Resistor [tolerance=±5% resistance=1k package=THT]
  Q1 = NPN-Transistor [part_number=2n3904 package="SOT-23 [SMD]"]
  M1 = DC Motor

nets:
  N1: Raspberry_Pi1.GPIO18, R1.Pin_1
  N2: Raspberry_Pi1.GND, Q1.2
  N3: Raspberry_Pi1.5V, M1.pin_2
  N4: R1.Pin_0, Q1.0
  N5: Q1.1, M1.pin_1
