# Fritzing sketch fan_manager_full_circuit (saved by Fritzing 0.9.3b)
breadboards: 1

parts:
  Raspberry_Pi1 = Raspberry Pi B+
  R1 = Resistor [tolerance=±5% resistance=1k package=THT]
  Q1 = NPN-Transistor [part_number=2n3904 package="SOT-23 [SMD]"]
  M1 = DC Motor
  S1 = Toggle Switch [package=THT]
  S2 = Toggle Switch [package=THT]

nets:
  N1: Raspberry_Pi1.3v3, S2.L2
  N2: Raspberry_Pi1.GPIO18, S1.L1
  N3: Raspberry_Pi1.GND, Q1.2
  N4: Raspberry_Pi1.5V, M1.pin_2
  N5: R1.Pin_0, Q1.0
  N6: R1.Pin_1, S1.COM
  N7: Q1.1, M1.pin_1
  N8: S1.L2, S2.COM
